# Fritzing sketch TeoG (saved by Fritzing 0.9.3b)

parts:
  Componente1 = Arduino Mega 2560 (Rev3)
  C1 = Ceramic Capacitor [capacitance=10µF voltage=6.3V package="100 mil [THT, multilayer]"]  # not connected
  R2 = Resistor [tolerance=±5% resistance=1k package=THT]
  R1 = Resistor [tolerance=±5% resistance=1k package=THT]

nets:
  N1: Componente1.D17_PWM/RX2, R2.Pin_0
  N2: Componente1.D16_PWM/TX2, R1.Pin_0

notes:
  Shield 1 motore 1
  m1pwm
  4
  m1dir
  50
  m1fb
  a7
  d2
  48
  sf
  52
  Shield 2 motore 2 e 3
  m2pwm
  12
  m3pwm
  13
  m2dir
  46
  m3dir
  40
  m2fb
  a6
  m3fb
  a5
  d2
  10
  sf
  11
  Encoders
  Encoder 1
  Encoder 2
  Encoder 3
  pin A
  2
  18
  21
  pin B
  3
  19
  20
  Sonar
  Sonar 1
  Sonar 2
  Sonar 3
  Sonar 4
  DX
  FRONT
  SX
  BEHIND
  Trig
  26
  30
  34
  36
  Echo
  24
  28
  32
  38
  SD Reader
  tx
  17
  rx
  16
  Busy
  5
  Bluetooth
  tx
  15
  rx
  14
  voltage checker
  A4
  Head Led
  9
  micro
  A11
  Capacitivi abbraccio
  send
  reciver
  front
  45
  43
  sx
  53
  51
  dx
  49
  47
  res 1MΩ
  capacitivi testa
  send
  reciver
  button0
  27
  29
  button1
  31
  33
  button2
  35
  37
  button3
  39
  41
  LED BASE
  R 6
  G 7
  B 8
  1kΩ
